# Fritzing sketch roomba_wall_v2 (saved by Fritzing 0.9.2b)
breadboards: 1

parts:
  U1 = attiny85 [package=dip]
  S2 = SPST Switch [package=switch-spdt_kit]
  Q1 = NPN-Transistor [package="TO92 [THT]"]
  LED1 = LED - 5mm [color="Infrared (940nm)" package="5 mm [THT]"]
  LED2 = LED - 5mm [color="Red (633nm)" package="5 mm [THT]"]
  R1 = Resistor [tolerance=±5% resistance=470 package="2512 [SMD]"]
  R2 = Resistor [tolerance=±5% resistance=47 package="2512 [SMD]"]
  R3 = Resistor [tolerance=±5% resistance=470 package="2512 [SMD]"]
  Y1 = Resonator [frequency="8 MHz" package=THT]
  VCC1 = Battery

nets:
  N1: U1.Pin_2, Y1.0
  N2: U1.Pin_3, Y1.pin_1
  N3: U1.Pin_4, Q1.B, LED2.cathode, Y1.GND, VCC1.-
  N4: U1.Pin_5, R1.Pin_0
  N5: U1.Pin_6, R3.Pin_0
  N6: U1.Pin_8, S2.S
  N7: S2.P, R2.Pin_0, VCC1.+
  N8: Q1.E, LED1.cathode
  N9: Q1.C, R3.Pin_1
  N10: LED1.anode, R2.Pin_1
  N11: LED2.anode, R1.Pin_1
